# Fritzing sketch Arduino (saved by Fritzing 0.9.3b)
breadboards: 1

parts:
  Componente1 = Arduino Uno (Rev3) - ICSP
  LED1 = RGB LED (com. cathode, rgb) [package="5 mm [THT]"]
  R1 = Photocell (LDR) [package=THT]
  R2 = Resistor [tolerance=±5% resistance=10k package=THT]
  R3 = Resistor [tolerance=±5% resistance=10k package=THT]
  R6 = Resistor [tolerance=±5% resistance=10k package=THT]
  R7 = Resistor [tolerance=±5% resistance=10k package=THT]

nets:
  GND: Componente1.GND, LED1.common_cathode, R3.Pin_1
  N1: Componente1.D9_PWM, R1.pin_1, R3.Pin_0
  N2: Componente1.D3_PWM, R6.Pin_1
  N3: Componente1.D5_PWM, R7.Pin_1
  N4: Componente1.D6_PWM, R2.Pin_1
  N5: Componente1.5V, R1.pin_0
  5V: Componente1.VIN
  N6: LED1.red_anode, R2.Pin_0
  N7: LED1.green_anode, R7.Pin_0
  N8: LED1.blue_anode, R6.Pin_0
