# Fritzing sketch ESP32 (saved by Fritzing 0.9.3b)
breadboards: 1

parts:
  M1 = DOIT Esp32 DevKit v1 (30 pins long, 11 pins width) [part_number=ESP32S-PIN30]
  R1 = Resistor [tolerance=±5% resistance=510 package=THT]
  R2 = Resistor [tolerance=±5% resistance=1k package=THT]
  R3 = Photocell (LDR) [package=THT]
  LED1 = RGB LED (com. anode, rbg) [package="5 mm [THT]"]

nets:
  N1: M1.3V3, LED1.common_anode
  N2: M1.D32, LED1.red_cathode
  N3: M1.D33, LED1.blue_cathode
  N4: M1.D25, LED1.green_cathode
  N5: M1.D27, R2.Pin_1, R3.pin_0
  GND: M1.GND, R1.Pin_1
  5V: M1.VIN, R3.pin_1
  N6: R1.Pin_0, R2.Pin_0

custom parts:
  DOIT Esp32 DevKit v1 (30 pins long, 11 pins width): The DOIT Esp32 DevKit v1 is one of the development board created by DOIT to evaluate the ESP-WROOM-32 module. It is based on the ESP32 microcontroller that boasts Wifi, Bluetooth, Ethernet and Low Power support all in a single chip. (vanepp) made breadboard work, adjusted pin numbering and labels and reduced size of schematic and cleaned up pcb. This chip is 30pins long (2 x15) and 11 pins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
